// Logisim project Clase24919.circ as structural Verilog: 1 circuit, main circuit main
module main (
  input  in_1,
  input  A,
  input  B,
  input  in_4,
  input  C,
  output out_6,
  output out_7,
  output out_8,
  output out_9,
  output out_10,
  output out_11,
  output out_12
);

  wire not_2_out, or_2_out;

  not not_1 (out_6, in_1);
  or or_1 (out_7, in_1, in_4);
  and and_1 (out_9, in_1, in_4);
  nor nor_1 (out_10, in_1, in_4);
  nand nand_1 (out_11, in_1, in_4);
  xor xor_1 (out_12, in_1, in_4);
  not not_2 (not_2_out, C);
  or or_2 (or_2_out, A, B);
  and and_2 (out_8, or_2_out, not_2_out);

  // Notes on the sheet:
  //   Ejemplo de clase x= (a+b)*c\
endmodule
