// Logisim project Practica1.4.circ as structural Verilog: 1 circuit, main circuit main
module main (
  input  in_1,
  input  in_2,
  input  in_3,
  input  in_4,
  input  in_5,
  input  in_6,
  input  in_7,
  input  in_8,
  input  in_9,
  input  [3:0] in_10,
  input  in_11,
  input  in_12,
  input  in_13,
  input  [1:0] in_14,
  input  [7:0] in_15,
  input  [2:0] in_16,
  input  in_17,
  input  [1:0] in_18,
  output [2:0] out_19,
  output out_20,
  output out_21,
  output out_22,
  output out_23,
  output out_24,
  output out_25,
  output out_26,
  output out_27,
  output out_28,
  output out_29,
  output out_30,
  output out_31,
  output out_32,
  output out_33
);

  wire clock_1_out, clock_2_out, decoder_1_out0, decoder_1_out5, decoder_1_out10, decoder_1_out15,
       j_k_ff_2_q, j_k_ff_4_q, j_k_ff_6_q, or_1_out;

  Demultiplexer #(.select(2), .enable("false")) demultiplexer_1 (
    .out0(out_26), .out1(out_27), .out2(out_28), .out3(out_29), .in(in_17), .sel(in_18));
  Priority_Encoder priority_encoder_1 (
    .in0(in_1), .in1(in_2), .in2(in_3), .in3(in_4), .in4(in_5), .in5(in_6), .in6(in_7), .in7(in_8),
    .out(out_19));  // open: en_in, gs, en_out
  Multiplexer #(.select(2), .enable("false")) multiplexer_1 (
    .in0(in_9), .in1(in_11), .in2(in_12), .in3(in_13), .out(out_20), .sel(in_14));
  Hex_Digit_Display hex_digit_display_1 (.value(in_10));  // open: dp
  Decoder #(.select(4), .enable("false")) decoder_1 (
    .out0(decoder_1_out0), .out5(decoder_1_out5), .out10(decoder_1_out10), .out15(decoder_1_out15),
    .sel(in_10));  // open: out1, out2, out3, out4, out6, out7, out8, out9, out11, out12, out13, out14
  BitSelector bitselector_1 (.in(in_15), .out(out_25), .sel(in_16));
  Clock clock_1 (.out(clock_1_out));
  LED led_1 (.in(or_1_out));
  or or_1 (or_1_out, decoder_1_out0, decoder_1_out5, decoder_1_out10, decoder_1_out15);
  Clock clock_2 (.out(clock_2_out));
  J_K_Flip_Flop #(.trigger("falling")) j_k_ff_1 (
    .J(1'b1), .clk(clock_1_out), .K(1'b1), .Q(out_33));  // open: Qn, preset, en, reset
  J_K_Flip_Flop j_k_ff_2 (
    .J(1'b1), .clk(clock_2_out), .K(1'b1), .Q(j_k_ff_2_q), .Qn(out_24));  // open: preset, en, reset
  J_K_Flip_Flop #(.trigger("falling")) j_k_ff_3 (
    .J(1'b1), .clk(out_33), .K(1'b1), .Q(out_32));  // open: Qn, preset, en, reset
  J_K_Flip_Flop j_k_ff_4 (
    .J(1'b1), .clk(j_k_ff_2_q), .K(1'b1), .Q(j_k_ff_4_q), .Qn(out_23));  // open: preset, en, reset
  J_K_Flip_Flop #(.trigger("falling")) j_k_ff_5 (
    .J(1'b1), .clk(out_32), .K(1'b1), .Q(out_31));  // open: Qn, preset, en, reset
  J_K_Flip_Flop j_k_ff_6 (
    .J(1'b1), .clk(j_k_ff_4_q), .K(1'b1), .Q(j_k_ff_6_q), .Qn(out_22));  // open: preset, en, reset
  J_K_Flip_Flop #(.trigger("falling")) j_k_ff_7 (
    .J(1'b1), .clk(out_31), .K(1'b1), .Q(out_30));  // open: Qn, preset, en, reset
  J_K_Flip_Flop j_k_ff_8 (.J(1'b1), .clk(j_k_ff_6_q), .K(1'b1), .Qn(out_21));  // open: Q, preset, en, reset

  // Notes on the sheet:
  //   CODIFICADOR DE 3 BITS
  //   EJERCICIO2
  //   EJERCICIO 3
  //   EJERCICIO 5
  //   EJERCICIO 4
  //   EJERCICIO 12
  //   EJERCICIO 12
endmodule
