// Logisim project Practica1.3.circ as structural Verilog: 1 circuit, main circuit main
module main (
  input  in_1,
  input  in_2,
  input  in_3,
  input  in_4,
  input  A,
  input  B,
  input  C,
  input  A_2,
  input  B_2,
  input  C_2,
  input  A_3,
  input  B_3,
  input  C_3,
  input  A_4,
  input  B_4,
  input  C_4,
  input  D,
  output out_18,
  output out_19,
  output out_20,
  output out_21,
  output out_22,
  output out_23,
  output out_24,
  output out_25
);

  wire and_2_out, and_3_out, and_4_out, and_5_out, nand_1_out, nand_2_out, nand_3_out, nor_1_out, nor_2_out,
       not_1_out, not_2_out, not_3_out, or_1_out, or_2_out, or_3_out, or_7_out, transistor_1_out;

  Transistor #(.\type ("n")) transistor_1 (.in(1'b1), .out(transistor_1_out), .gate(in_1));
  Transistor #(.\type ("n"), .gate("br")) transistor_2 (.in(1'b1), .out(out_20), .gate(in_4));
  Transistor #(.\type ("n")) transistor_3 (.in(transistor_1_out), .out(out_19), .gate(in_2));
  Pull_Resistor pull_resistor_1 (.node(out_19));
  Transistor #(.\type ("n")) transistor_4 (.in(1'b1), .out(out_20), .gate(in_3));
  Pull_Resistor pull_resistor_2 (.node(out_20));
  not not_1 (not_1_out, B);
  not not_2 (not_2_out, C_2);
  or or_1 (or_1_out, A, B, not_1_out);
  nand nand_1 (nand_1_out, A, B);
  or or_2 (or_2_out, A_2, B_2);
  nand nand_2 (nand_2_out, A_2, C_2);
  nor nor_1 (nor_1_out, A_3, C_3);
  nand nand_3 (nand_3_out, A_3, B_3, C_3);
  nor nor_2 (nor_2_out, B_4, C_4);
  not not_3 (not_3_out, B_4);
  buf and_1 (out_18, in_2);  // AND_Gate
  and and_2 (and_2_out, or_2_out, nand_2_out);
  and and_3 (and_3_out, B_2, not_2_out);
  xor xor_1 (out_24, nor_1_out, nand_3_out);
  or or_3 (or_3_out, nor_2_out, A_4);
  and and_4 (and_4_out, A_4, not_3_out);
  and and_5 (and_5_out, A_4, D);
  or or_4 (out_21, in_3, in_4);
  or or_5 (out_22, or_1_out, nand_1_out);
  or or_6 (out_23, and_2_out, and_3_out);
  or or_7 (or_7_out, and_4_out, and_5_out);
  nor nor_3 (out_25, or_3_out, or_7_out);

  assign C = B;

  // Notes on the sheet:
  //   Ejercicio 1 y 2
  //   Ejercicio 3
  //   a)
  //   b)
  //   c)
  //   d)
  //   Circuito AND
  //   Circuito OR
endmodule
